// Logisim project MpMp25.circ as structural Verilog: 8 circuits, main circuit main
module main (
  input  RST
);

  wire ALU_AccuEn, ALU_CE, ALU_F_E, and_2_out, and_3_out, and_4_out, and_5_out, CLK, CLK_E, clock_1_out,
       cu_1_clk_qtr, cu_1_io_input, cu_1_lng_jmp, cu_1_lng_jmp_r, cu_1_rf_ce0, cu_1_rf_ce1,
       cu_1_rf_data_out_0_e, cu_1_rf_pt_e, cu_1_rf_w_nr, decoder_1_out0, decoder_1_out1, decoder_1_out2,
       decoder_1_out3, decoder_1_out4, decoder_1_out5, decoder_2_out0, decoder_2_out1, decoder_2_out2,
       decoder_2_out3, decoder_2_out4, decoder_2_out5, decoder_2_out6, decoder_3_out0, decoder_3_out1,
       decoder_3_out7, nor_1_out, or_1_out, PC_OVF, RAM_CE, RAM_WE, switch_1_p1;
  wire [0:0] keyboard_1_avail;
  wire [2:0] cu_1_reg0, cu_1_reg1;
  wire [3:0] ALU_CMD, joystick_1_x, joystick_1_y;
  wire [6:0] cu_1_const, keyboard_1_data;
  wire [7:0] Addr, alu_1_flag_out, alu_1_result, ALU_F_IN, DBG_LED, IO_8_B_q, IO_9_G_q, IO_a_R_q, IO_D_X_q,
       IO_F_Y_q, MEM_PAGE, PC, pull_resistor_2_node, ram_1_dout, register_2_q, rf_1_data_out0, rom_1_data;
  wire [7:7] cu_1_const_2;
  wire [15:0] register_1_q, rom_2_data;

  Clock clock_1 (.out(clock_1_out));
  and and_1 (CLK, ~CLK_E, clock_1_out);  // AND_Gate
  CU cu_1 (
    .CLK(CLK), .RST(RST), .Instruction(rom_2_data), .ALU_F_IN(ALU_F_IN), .Reg0(cu_1_reg0), .Reg1(cu_1_reg1),
    .\const ({cu_1_const_2[7], cu_1_const}), .RF_W_nR(cu_1_rf_w_nr), .RF_CE0(cu_1_rf_ce0),
    .RF_CE1(cu_1_rf_ce1), .ALU_AccuEn(ALU_AccuEn), .ALU_CE(ALU_CE), .RAM_WE(RAM_WE), .RAM_CE(RAM_CE),
    .ALU_CMD(ALU_CMD), .RF_PT_E(cu_1_rf_pt_e), .CLK_QTR(cu_1_clk_qtr),
    .RF_Data_Out_0_E(cu_1_rf_data_out_0_e), .IO_Input(cu_1_io_input), .ADDR(Addr), .ALU_F_E(ALU_F_E),
    .LNG_JMP(cu_1_lng_jmp), .LNG_JMP_R(cu_1_lng_jmp_r));  // open: RegResult
  assign {cu_1_const_2[7], cu_1_const} = cu_1_lng_jmp ? {{5{1'b0}}, cu_1_reg0} : 8'bz;  // Controlled_Buffer controlled_buffer_1
  assign Addr = cu_1_lng_jmp ? 8'hf9 : 8'bz;  // Controlled_Buffer controlled_buffer_2
  assign Addr = cu_1_lng_jmp_r ? 8'hf9 : 8'bz;  // Controlled_Buffer controlled_buffer_3
  Register #(.width(16)) register_1 (.Q(register_1_q));  // open: D, en, clk, clr
  // Switch switch_1: pin names not known; wires that end beside it: switch_1_p1, CLK_E
  Comparator #(.width(16)) comparator_1 (.a(register_1_q), .b({MEM_PAGE, PC}), .eq(switch_1_p1));  // open: gt, lt
  RF rf_1 (
    .Addr0(cu_1_reg0), .Addr1(cu_1_reg1), .Data_In({cu_1_const_2[7], cu_1_const}), .W_nR(cu_1_rf_w_nr),
    .CE0(cu_1_rf_ce0), .CE1(cu_1_rf_ce1), .CLK(CLK), .RST(RST), .PTR_E(cu_1_rf_pt_e), .CLK_QTR(cu_1_clk_qtr),
    .Data_OUT0(rf_1_data_out0), .Data_OUT1({cu_1_const_2[7], cu_1_const}), .PC(PC), .PointerReg(Addr),
    .PC_OVF(PC_OVF));
  ROM rom_1 (.addr(Addr), .data(rom_1_data));
  Hex_Digit_Display hex_digit_display_1 (.value(register_1_q[15:12]));  // open: dp
  Hex_Digit_Display hex_digit_display_2 (.value(register_1_q[11:8]));  // open: dp
  Pull_Resistor pull_resistor_1 (.node(CLK_E));
  Hex_Digit_Display hex_digit_display_3 (.value(MEM_PAGE[7:4]));  // open: dp
  Hex_Digit_Display hex_digit_display_4 (.value(register_1_q[7:4]));  // open: dp
  Hex_Digit_Display hex_digit_display_5 (.value(register_1_q[3:0]));  // open: dp
  Hex_Digit_Display hex_digit_display_6 (.value(MEM_PAGE[3:0]));  // open: dp
  Hex_Digit_Display hex_digit_display_7 (.value(PC[7:4]));  // open: dp
  ROM #(.addrWidth(16), .dataWidth(16)) rom_2 (.addr({MEM_PAGE, PC}), .data(rom_2_data));
  Hex_Digit_Display hex_digit_display_8 (.value(PC[3:0]));  // open: dp
  ALU alu_1 (
    .Flag_In(ALU_F_IN), .CMD_15_12(ALU_CMD), .Op0(rf_1_data_out0), .Op1({cu_1_const_2[7], cu_1_const}),
    .Result(alu_1_result), .Flag_Out(alu_1_flag_out));
  Decoder #(.select(3)) decoder_1 (
    .out0(decoder_1_out0), .out1(decoder_1_out1), .out2(decoder_1_out2), .out3(decoder_1_out3),
    .out4(decoder_1_out4), .out5(decoder_1_out5), .sel(Addr[2:0]), .en(and_2_out));  // open: out6, out7
  and and_2 (and_2_out, ~Addr[3], ~Addr[4], ~Addr[5], ~Addr[6], ~Addr[7], cu_1_io_input);  // AND_Gate
  and and_3 (and_3_out, Addr[3], ~Addr[4], ~Addr[5], ~Addr[6], ~Addr[7], cu_1_io_input);  // AND_Gate
  nor nor_1 (nor_1_out, and_3_out, and_4_out);
  and and_4 (and_4_out, Addr[3], Addr[4], Addr[5], Addr[6], Addr[7], cu_1_io_input);
  // LedBar #(.inputtype("row")) ledbar_1: pin names not known; wires that end beside it: DBG_LED
  assign {cu_1_const_2[7], cu_1_const} = ALU_CE ? register_2_q : 8'bz;  // Controlled_Buffer controlled_buffer_4
  Register register_2 (.D(alu_1_result), .en(ALU_AccuEn), .Q(register_2_q), .clk(CLK), .clr(RST));
  Decoder #(.select(3)) decoder_2 (
    .out0(decoder_2_out0), .out1(decoder_2_out1), .out2(decoder_2_out2), .out3(decoder_2_out3),
    .out4(decoder_2_out4), .out5(decoder_2_out5), .out6(decoder_2_out6), .sel(Addr[2:0]), .en(and_3_out));  // open: out7
  assign {cu_1_const_2[7], cu_1_const} = and_5_out ? rom_1_data : 8'bz;  // Controlled_Buffer controlled_buffer_5
  and and_5 (and_5_out, nor_1_out, cu_1_io_input);
  Decoder #(.select(3)) decoder_3 (
    .out0(decoder_3_out0), .out1(decoder_3_out1), .out7(decoder_3_out7), .sel(Addr[2:0]), .en(and_4_out));  // open: out2, out3, out4, out5, out6
  assign {cu_1_const_2[7], cu_1_const} = cu_1_rf_data_out_0_e ? rf_1_data_out0 : 8'bz;  // Controlled_Buffer controlled_buffer_6
  Pull_Resistor pull_resistor_2 (.node(pull_resistor_2_node));
  assign pull_resistor_2_node = decoder_3_out7 ? {cu_1_const_2[7], cu_1_const} : 8'bz;  // Controlled_Buffer controlled_buffer_7
  RAM ram_1 (.addr(Addr), .we(RAM_WE), .oe(RAM_CE), .clk(CLK), .din({cu_1_const_2[7], cu_1_const}), .dout(ram_1_dout));
  TTY tty_1 (.data(cu_1_const), .clk(CLK), .we(decoder_1_out0), .clr(decoder_1_out1));
  Keyboard keyboard_1 (
    .clk(CLK), .re(decoder_1_out2), .clr(decoder_1_out4), .avail(keyboard_1_avail[0]), .data(keyboard_1_data));
  Register IO_8_B (.D({cu_1_const_2[7], cu_1_const}), .en(decoder_2_out0), .Q(IO_8_B_q), .clk(CLK), .clr(RST));
  Register IO_9_G (.D({cu_1_const_2[7], cu_1_const}), .en(decoder_2_out1), .Q(IO_9_G_q), .clk(CLK), .clr(RST));
  Register IO_a_R (.D({cu_1_const_2[7], cu_1_const}), .en(decoder_2_out2), .Q(IO_a_R_q), .clk(CLK), .clr(RST));
  Register IO_D_X (.D({cu_1_const_2[7], cu_1_const}), .en(decoder_2_out5), .Q(IO_D_X_q), .clk(CLK), .clr(RST));
  Register IO_F_Y (.D({cu_1_const_2[7], cu_1_const}), .en(decoder_2_out6), .Q(IO_F_Y_q), .clk(CLK), .clr(RST));
  Counter #(.trigger("falling")) counter_1 (
    .load(decoder_3_out1), .D({cu_1_const_2[7], cu_1_const}), .count(PC_OVF), .Q(MEM_PAGE), .up(1'b1),
    .clk(CLK), .clr(RST));  // open: carry
  S_R_Flip_Flop s_r_ff_1 (.S(pull_resistor_2_node[0]), .clk(CLK), .R(RST), .Q(DBG_LED[0]));  // open: Qn, preset, reset
  S_R_Flip_Flop s_r_ff_2 (.S(pull_resistor_2_node[1]), .clk(CLK), .R(RST), .Q(DBG_LED[1]));  // open: Qn, preset, reset
  S_R_Flip_Flop s_r_ff_3 (.S(pull_resistor_2_node[2]), .clk(CLK), .R(RST), .Q(DBG_LED[2]));  // open: Qn, preset, reset
  S_R_Flip_Flop s_r_ff_4 (.S(pull_resistor_2_node[3]), .clk(CLK), .R(RST), .Q(DBG_LED[3]));  // open: Qn, preset, reset
  S_R_Flip_Flop s_r_ff_5 (.S(pull_resistor_2_node[4]), .clk(CLK), .R(RST), .Q(DBG_LED[4]));  // open: Qn, preset, reset
  S_R_Flip_Flop s_r_ff_6 (.S(pull_resistor_2_node[5]), .clk(CLK), .R(RST), .Q(DBG_LED[5]));  // open: Qn, preset, reset
  S_R_Flip_Flop s_r_ff_7 (.S(pull_resistor_2_node[6]), .clk(CLK), .R(RST), .Q(DBG_LED[6]));  // open: Qn, preset, reset
  S_R_Flip_Flop s_r_ff_8 (.S(pull_resistor_2_node[7]), .clk(CLK), .R(RST), .Q(DBG_LED[7]));  // open: Qn, preset, reset
  Register register_3 (.D(alu_1_flag_out), .en(ALU_F_E), .Q(ALU_F_IN), .clk(CLK), .clr(RST));
  assign {cu_1_const_2[7], cu_1_const} = decoder_3_out0 ? MEM_PAGE : 8'bz;  // Controlled_Buffer controlled_buffer_8
  or or_1 (or_1_out, RST, decoder_2_out3);
  assign {cu_1_const_2[7], cu_1_const} = RAM_CE ? ram_1_dout : 8'bz;  // Controlled_Buffer controlled_buffer_9
  assign {cu_1_const_2[7], cu_1_const} = decoder_1_out2 ? {1'b0, keyboard_1_data} : 8'bz;  // Controlled_Buffer controlled_buffer_10
  assign {cu_1_const_2[7], cu_1_const} = decoder_1_out3 ? {{7{1'b0}}, keyboard_1_avail[0]} : 8'bz;  // Controlled_Buffer controlled_buffer_11
  // RGB_Video #(.height(256), .width(256)) rgb_video_1: pin names not known; wires that end beside it: or_1_out, CLK, decoder_2_out4, IO_D_X_q, IO_F_Y_q, {IO_a_R_q, IO_9_G_q, IO_8_B_q}
  Joystick joystick_1 (.x(joystick_1_x), .y(joystick_1_y));
  assign {cu_1_const_2[7], cu_1_const} = decoder_1_out5 ? {joystick_1_y, joystick_1_x} : 8'bz;  // Controlled_Buffer controlled_buffer_12

  // Notes on the sheet:
  //   Instruction bus
  //   unused
  //   Data bus
  //   contents of rom_2 (hex, n*v repeats v):
  //   fa80 fb80 fc01 fd01 fe02 8a00 506*0 de08 dd09 dc0a db0e da0d d80b
  //   i/O Input
  //   Instruction BUS
  //   CE
  //   blank
  //   strope
  //   Page Registe I/O Addr. 9
  //   Paging Register
  //   256 Worte x 256 Seiten
  //   Pages: 0...FF, 100...1FF, ...
  //   in Hexanzeige von Program Memory dann 0100, wenn auf nächster Seite
  //   damit 65 kB RAM
  //   DATA BUS
endmodule

module ALU (
  input  [7:0] Op0,
  input  [7:0] Op1,
  input  [3:0] CMD_15_12,
  input  [7:0] Flag_In,
  output [7:0] Result,
  output [7:0] Flag_Out
);

  wire adder_1_cout, adder_2_cout, comparator_2_eq, multiplexer_1_out, multiplexer_3_out, multiplexer_4_out,
       R, shiftl_1_cout, subtractor_1_bout, subtractor_2_bout, xor_2_out, Z_out;
  wire [0:0] undriven;
  wire [7:0] adder_1_out, adder_2_out, and_1_out, divider_1_out, divider_1_rem, Flag_Select_data,
       multiplier_1_out, negator_1_out, not_1_out, or_1_out, shiftl_1_result, subtractor_1_out,
       subtractor_2_out, xnor_1_out, xor_1_out;
  wire [9:0] shifter_1_out;

  Adder adder_1 (.a(Op0), .b(Op1), .out(adder_1_out), .cout(adder_1_cout));  // open: cin
  Subtractor subtractor_1 (.a(Op1), .b(Op0), .out(subtractor_1_out), .bout(subtractor_1_bout));  // open: bin
  Multiplier multiplier_1 (.a(Op0), .b(Op1), .out(multiplier_1_out));  // open: cin, cout
  Divider divider_1 (.a(Op1), .b(Op0), .out(divider_1_out), .upper({8{1'b0}}), .rem(divider_1_rem));
  Negator negator_1 (.in(Op1), .out(negator_1_out));
  assign and_1_out = Op1 & Op0;  // AND_Gate and_1, 8 bits wide
  assign or_1_out = Op1 | Op0;  // OR_Gate or_1, 8 bits wide
  assign xor_1_out = Op1 ^ Op0;  // XOR_Gate xor_1, 8 bits wide
  assign xnor_1_out = ~(Op0 ^ Op1);  // XNOR_Gate xnor_1, 8 bits wide
  assign not_1_out = ~Op1;  // NOT_Gate not_1, 8 bits wide
  Adder adder_2 (.a(Op1), .b(Op0), .out(adder_2_out), .cin(Flag_In[1]), .cout(adder_2_cout));
  Subtractor subtractor_2 (.a(Op1), .b(Op0), .out(subtractor_2_out), .bin(Flag_In[1]), .bout(subtractor_2_bout));
  ROM #(.addrWidth(4)) Flag_Select (.addr(CMD_15_12), .data(Flag_Select_data));
  Comparator comparator_1 (.a({8{1'b0}}), .b(divider_1_rem), .gt(R));  // open: eq, lt
  ShiftL shiftl_1 (.Op(Op1), .Dist(Op0), .CIn(Flag_In[1]), .Result(shiftl_1_result), .COut(shiftl_1_cout));
  Shifter #(.shift("lr"), .width(10)) shifter_1 (
    .in({Flag_In[1], Op1, undriven[0]}), .\dist (Op0[3:0]), .out(shifter_1_out));
  Comparator comparator_2 (.a(Op0), .b({8{1'b0}}), .eq(comparator_2_eq));  // open: gt, lt
  Multiplexer #(.select(4)) multiplexer_1 (
    .in0(Flag_In[3]), .in1(Flag_In[3]), .in2(Flag_In[3]), .in3(comparator_2_eq), .in4(Flag_In[3]),
    .in5(Flag_In[3]), .in6(Flag_In[3]), .in7(Flag_In[3]), .in8(Flag_In[3]), .in9(Flag_In[3]),
    .in10(Flag_In[3]), .in11(Flag_In[3]), .in12(Flag_In[3]), .in13(Flag_In[3]), .in14(Flag_In[3]),
    .in15(Flag_In[3]), .out(multiplexer_1_out), .sel(CMD_15_12));
  xor xor_2 (xor_2_out, Result[7], Op1[7]);
  Multiplexer #(.select(4), .width(8)) multiplexer_2 (
    .in0(adder_1_out), .in1(subtractor_1_out), .in2(multiplier_1_out), .in3(divider_1_out),
    .in4(shiftl_1_result), .in5(shifter_1_out[8:1]), .in6(negator_1_out), .in7({8{1'b0}}), .in8({8{1'b0}}),
    .in9(and_1_out), .in10(or_1_out), .in11(xor_1_out), .in12(xnor_1_out), .in13(not_1_out),
    .in14(adder_2_out), .in15(subtractor_2_out), .out(Result), .sel(CMD_15_12));
  Multiplexer #(.select(4)) multiplexer_3 (
    .in0(adder_1_cout), .in1(subtractor_1_bout), .in2(Flag_In[1]), .in3(Flag_In[1]), .in4(shiftl_1_cout),
    .in5(shifter_1_out[9]), .in6(Flag_In[1]), .in7(Flag_In[1]), .in8(Flag_In[1]), .in9(Flag_In[1]),
    .in10(Flag_In[1]), .in11(Flag_In[1]), .in12(Flag_In[1]), .in13(Flag_In[1]), .in14(adder_2_cout),
    .in15(subtractor_2_bout), .out(multiplexer_3_out), .sel(CMD_15_12));
  Multiplexer #(.select(4)) multiplexer_4 (
    .in0(xor_2_out), .in1(xor_2_out), .in2(xor_2_out), .in3(Flag_In[2]), .in4(Flag_In[2]), .in5(Flag_In[2]),
    .in6(Flag_In[2]), .in7(Flag_In[2]), .in8(Flag_In[2]), .in9(Flag_In[2]), .in10(Flag_In[2]),
    .in11(Flag_In[2]), .in12(Flag_In[2]), .in13(Flag_In[2]), .in14(xor_2_out), .in15(xor_2_out),
    .out(multiplexer_4_out), .sel(CMD_15_12));
  // Probe on Result
  Multiplexer multiplexer_5 (.in0(Flag_In[0]), .in1(Z_out), .out(Flag_Out[0]), .sel(Flag_Select_data[0]));
  Multiplexer multiplexer_6 (.in0(Flag_In[1]), .in1(multiplexer_3_out), .out(Flag_Out[1]), .sel(Flag_Select_data[1]));
  Multiplexer multiplexer_7 (.in0(Flag_In[2]), .in1(multiplexer_4_out), .out(Flag_Out[2]), .sel(Flag_Select_data[2]));
  Multiplexer multiplexer_8 (.in0(Flag_In[3]), .in1(multiplexer_1_out), .out(Flag_Out[3]), .sel(Flag_Select_data[3]));
  Multiplexer multiplexer_9 (.in0(Flag_In[4]), .in1(R), .out(Flag_Out[4]), .sel(Flag_Select_data[4]));
  nor Z (Z_out, Result[0], Result[1], Result[2], Result[3], Result[4], Result[5], Result[6], Result[7]);

  assign Flag_Out[7:5] = Flag_In[7:5];

  // Other names for the same wires on the sheet: Op1_Tunnel[7:0] = Op1; C = Flag_In[1]; Op0_Tunnel[7:0] = Op0

  // Notes on the sheet:
  //   ADD 0, SUB 1, ADDC 14; SUBC 15
  //   ADD 0x00, SUB 0x01, ADDC 0x0E; SUBC 0x0F
  //   Op0
  //   Op1
  //   Op1 kommt immer zuerst; guck in Git!
  //   contents of Flag_Select (hex, n*v repeats v):
  //   7 7 5 19 3 3 1 0 0 5*1 7 7
  //   E_Flag
  //   R_Flag
  //   Z_Flag
  //   C_Flag
  //   O_Flag
  //     XXX,overflow_O, carry_C, zero_Z
  //   C_Flag
  //   O_Flag
  //   Z_Flag
  //   C_Flag
  //   O_Flag
  //   E_Flag
  //   R_Flag
endmodule

module CU (
  input  CLK,
  input  RST,
  input  [15:0] Instruction,
  input  [7:0] ALU_F_IN,
  output [2:0] Reg0,
  output [2:0] Reg1,
  output [2:0] RegResult,
  output [7:0] \const ,
  output RF_W_nR,
  output RF_CE0,
  output RF_CE1,
  output ALU_AccuEn,
  output ALU_CE,
  output RAM_WE,
  output RAM_CE,
  output [3:0] ALU_CMD,
  output RF_PT_E,
  output CLK_QTR,
  output RF_Data_Out_0_E,
  output IO_Input,
  output [7:0] ADDR,
  output ALU_F_E,
  output LNG_JMP,
  output LNG_JMP_R
);

  wire Cycle_Zero, multiplexer_1_out;
  wire [1:0] Cyclecounter_q, rom_1_data_3;
  wire [2:0] Reg0_t, Reg1_t, register_1_q, RegResult_t;
  wire [3:0] rom_1_data_2;
  wire [3:3] register_1_q_2;
  wire [6:4] and_2_out;
  wire [7:0] mc_const8, multiplexer_2_out;
  wire [9:9] xor_1_out;
  wire [11:6] IR_q;
  wire [23:7] rom_1_data;

  Counter #(.max('h3), .width(2)) Cyclecounter (
    .Q(Cyclecounter_q), .carry(CLK_QTR), .clk(CLK), .clr(RST));  // open: load, D, count, up
  Register #(.width(16)) IR (
    .D(Instruction), .en(Cycle_Zero), .Q({ALU_CMD, IR_q[11], RegResult_t, IR_q[7:6], Reg1_t, Reg0_t}),
    .clk(CLK), .clr(RST));
  Multiplexer #(.select(3)) multiplexer_1 (
    .in0(1'b0), .in1(ALU_F_IN[0]), .in2(ALU_F_IN[1]), .in3(ALU_F_IN[2]), .in4(ALU_F_IN[3]),
    .in5(ALU_F_IN[4]), .in6(ALU_F_IN[5]), .in7(ALU_F_IN[6]), .out(multiplexer_1_out), .sel(register_1_q));
  and and_1 (and_2_out[6], IR_q[7], ~IR_q[11]);  // AND_Gate
  and and_2 (and_2_out[4], ~IR_q[11], IR_q[6]);  // AND_Gate
  nor nor_1 (Cycle_Zero, Cyclecounter_q[0], Cyclecounter_q[1]);
  Multiplexer #(.width(8)) multiplexer_2 (
    .in0({{5{1'b0}}, Reg0_t}), .in1({IR_q[7:6], Reg1_t, Reg0_t}), .out(multiplexer_2_out), .sel(IR_q[11]));
  xor xor_1 (xor_1_out[9], multiplexer_1_out, register_1_q_2[3]);
  ROM #(.addrWidth(10), .dataWidth(32)) rom_1 (
    .addr({xor_1_out[9], and_2_out[6], IR_q[11], and_2_out[4], ALU_CMD, Cyclecounter_q}),
    .data({mc_const8, rom_1_data[23:22], LNG_JMP_R, rom_1_data[20], LNG_JMP, rom_1_data_2, ALU_F_E, rom_1_data[13], IO_Input, RF_Data_Out_0_E, rom_1_data_3[1], RF_PT_E, rom_1_data_3[0], rom_1_data[7], RAM_CE, RAM_WE, ALU_CE, ALU_AccuEn, RF_CE1, RF_CE0, RF_W_nR}));
  assign \const  = rom_1_data[7] ? multiplexer_2_out : 8'bz;  // Controlled_Buffer controlled_buffer_1
  Multiplexer #(.select(2), .width(3)) multiplexer_3 (
    .in0(RegResult_t), .in1(Reg0_t), .in2(Reg1_t), .out(Reg0), .sel(rom_1_data_3));  // open: in3
  assign ADDR = rom_1_data[13] ? multiplexer_2_out : 8'bz;  // Controlled_Buffer controlled_buffer_2
  assign ADDR = rom_1_data[20] ? mc_const8 : 8'bz;  // Controlled_Buffer controlled_buffer_3
  Register #(.width(4)) register_1 (
    .D(rom_1_data_2), .Q({register_1_q_2[3], register_1_q}), .clk(CLK), .clr(RST));  // open: en
  Multiplexer #(.width(3)) multiplexer_4 (.in0(Reg1_t), .in1(RegResult_t), .out(Reg1), .sel(rom_1_data_3[1]));

  // Notes on the sheet:
  //   IR
  //   Instruction Register
  //   IMOPb[7]
  //   IMOPa[11]
  //   CMD[6]
  //   CMD_const_8
  //   CMD0[15...12]
  //   2-0 Op0
  //   5-3 Op1
  //   10-8 RegR
  //   contents of rom_1 (hex, n*v repeats v):
  //   0 0 0 5 15*0 241 15*0 e22 13*0 201802 0 105 14*0 10e 11 0 0 10e 11 0 0 10e 11 0 0 10e 11 0 0 10e 11
  //   0 0 10e 11 0 0 10e 11 10*0 10e 11 0 0 10e 11 0 0 10e 11 0 0 10e 11 0 0 10e 11 0 0 10e 11 0 0 10e 11
  //   34*0 81000 581 0 0 8000 0 0 0 10000 0 0 0 8000 81 0 0 10000 81 0 0 0 3004 0 0 0 3002 0 0 0 81 487*0
  //   81 0 0 0 81
  //   09101802
  //   const_en
  //   Reg_ResOn0
  //   Reg_SLC
  //   Flag_Select_0
  //   Flag_Select_1
  //   Flag_Select_2
  //   Flag_neg
  //   mc_const8_E
  //   Addr_E
endmodule

module RF (
  input  [2:0] Addr0,
  input  [2:0] Addr1,
  input  [7:0] Data_In,
  input  W_nR,
  input  CE0,
  input  CE1,
  input  CLK,
  input  RST,
  input  PTR_E,
  input  CLK_QTR,
  output [7:0] Data_OUT0,
  output [7:0] Data_OUT1,
  output [7:0] PC,
  output [7:0] PointerReg,
  output PC_OVF
);

  wire and_1_out, and_2_out, decoder_1_out1, decoder_1_out2, decoder_1_out3, decoder_1_out4, decoder_1_out5,
       decoder_1_out6, decoder_1_out7, PC_OVF_t, PC_SLC;
  wire [7:0] register_1_q, register_2_q, register_3_q, register_4_q, register_5_q, register_6_q,
       Stack_Pointer_q;

  Decoder #(.select(3)) decoder_1 (
    .out0(PC_SLC), .out1(decoder_1_out1), .out2(decoder_1_out2), .out3(decoder_1_out3),
    .out4(decoder_1_out4), .out5(decoder_1_out5), .out6(decoder_1_out6), .out7(decoder_1_out7), .sel(Addr0),
    .en(W_nR));
  and and_1 (and_1_out, ~Addr0[0], ~Addr0[1], ~Addr0[2], W_nR);  // AND_Gate
  and and_2 (and_2_out, CLK_QTR, ~and_1_out);  // AND_Gate
  Counter #(.trigger("falling")) counter_1 (
    .load(PC_SLC), .D(Data_In), .count(and_2_out), .Q(PC), .carry(PC_OVF_t), .up(1'b1), .clk(CLK), .clr(RST));
  Register Stack_Pointer (.D(Data_In), .en(decoder_1_out1), .Q(Stack_Pointer_q), .clk(CLK), .clr(RST));
  Register register_1 (.D(Data_In), .en(decoder_1_out2), .Q(register_1_q), .clk(CLK), .clr(RST));
  Register register_2 (.D(Data_In), .en(decoder_1_out3), .Q(register_2_q), .clk(CLK), .clr(RST));
  Register register_3 (.D(Data_In), .en(decoder_1_out4), .Q(register_3_q), .clk(CLK), .clr(RST));
  Register register_4 (.D(Data_In), .en(decoder_1_out5), .Q(register_4_q), .clk(CLK), .clr(RST));
  Register register_5 (.D(Data_In), .en(decoder_1_out6), .Q(register_5_q), .clk(CLK), .clr(RST));
  Register register_6 (.D(Data_In), .en(decoder_1_out7), .Q(register_6_q), .clk(CLK), .clr(RST));
  Multiplexer #(.disabled("Z"), .enable("true"), .select(3), .width(8)) multiplexer_1 (
    .in0(PC), .in1(Stack_Pointer_q), .in2(register_1_q), .in3(register_2_q), .in4(register_3_q),
    .in5(register_4_q), .in6(register_5_q), .in7(register_6_q), .out(Data_OUT0), .sel(Addr0), .en(CE0));
  Multiplexer #(.disabled("Z"), .enable("true"), .select(3), .width(8)) multiplexer_2 (
    .in0(PC), .in1(Stack_Pointer_q), .in2(register_1_q), .in3(register_2_q), .in4(register_3_q),
    .in5(register_4_q), .in6(register_5_q), .in7(register_6_q), .out(Data_OUT1), .sel(Addr1), .en(CE1));
  Multiplexer #(.disabled("Z"), .enable("true"), .select(3), .width(8)) multiplexer_3 (
    .in0(PC), .in1(Stack_Pointer_q), .in2(register_1_q), .in3(register_2_q), .in4(register_3_q),
    .in5(register_4_q), .in6(register_5_q), .in7(register_6_q), .out(PointerReg), .sel(Addr1), .en(PTR_E));
  and and_3 (PC_OVF, PC_OVF_t, CLK_QTR, ~PC_SLC);  // AND_Gate

  // Notes on the sheet:
  //   Registerfile
  //   Speicherdecoder wann geschrieben wird
  //   Read notWrite
  //   Chipenable
  //   speicher in dem register sind 
  //   1
  //   6
  //   Pc
  //   2
  //   3
  //   4
  //   5
  //   7
endmodule

module test_ALU (
);

  wire and_1_out, and_2_out, clock_1_out, comparator_1_eq, comparator_2_eq;
  wire [3:0] ALU_Command_data;
  wire [7:0] alu_1_flag_out, alu_1_result, Flag_result_data, Flags_In_data, Op0_data, Op1_data, Result_data;
  wire [9:0] Adresse;

  Clock clock_1 (.out(clock_1_out));
  Hex_Digit_Display hex_digit_display_1 (.value({2'b00, Adresse[9:8]}));  // open: dp
  Hex_Digit_Display hex_digit_display_2 (.value(Adresse[7:4]));  // open: dp
  and and_1 (and_1_out, clock_1_out, and_2_out);
  Hex_Digit_Display hex_digit_display_3 (.value(Adresse[3:0]));  // open: dp
  Counter #(.max('h3ff), .trigger("falling"), .width(10)) counter_1 (
    .Q(Adresse), .clk(and_1_out));  // open: load, D, count, carry, up, clr
  ROM #(.addrWidth(10), .dataWidth(4)) ALU_Command (.addr(Adresse), .data(ALU_Command_data));
  ROM #(.addrWidth(10)) Op0 (.addr(Adresse), .data(Op0_data));
  ROM #(.addrWidth(10)) Op1 (.addr(Adresse), .data(Op1_data));
  ROM #(.addrWidth(10)) Result (.addr(Adresse), .data(Result_data));
  ALU alu_1 (
    .Flag_In(Flags_In_data), .Op0(Op0_data), .Op1(Op1_data), .Result(alu_1_result), .Flag_Out(alu_1_flag_out));  // open: CMD_15_12
  Comparator comparator_1 (.a(alu_1_result), .b(Result_data), .eq(comparator_1_eq));  // open: gt, lt
  ROM #(.addrWidth(10)) Flags_In (.addr(Adresse), .data(Flags_In_data));
  ROM #(.addrWidth(10)) Flag_result (.addr(Adresse), .data(Flag_result_data));
  Comparator comparator_2 (.a(Flag_result_data), .b(alu_1_flag_out), .eq(comparator_2_eq));  // open: gt, lt
  LED led_1 (.in(and_2_out));
  and and_2 (and_2_out, comparator_2_eq, comparator_1_eq);

  // Notes on the sheet:
  //   contents of Op0 (hex, n*v repeats v):
  //   1 2 3 aa ff
  //   contents of Op1 (hex, n*v repeats v):
  //   4 5 6 57 1
  //   contents of Result (hex, n*v repeats v):
  //   5 7 9 1
  //   CMD15_12
  //   Op1
  //   Result
  //   Op0
  //   Flag_In
  //   Flag_Out
  //   contents of Flag_result (hex, n*v repeats v):
  //   0 0 0 2 3
endmodule

module ShiftL (
  input  [7:0] Op,
  input  [7:0] Dist,
  input  CIn,
  output [7:0] Result,
  output COut
);

  wire comparator_1_eq;
  wire [3:0] subtractor_1_out;
  wire [8:0] shifter_1_out;

  Shifter #(.width(9)) shifter_1 (.in({Op, CIn}), .\dist (subtractor_1_out), .out(shifter_1_out));
  Subtractor #(.width(4)) subtractor_1 (.a(Dist[3:0]), .b(4'b0001), .out(subtractor_1_out));  // open: bin, bout
  Comparator comparator_1 (.a(Dist), .b({8{1'b0}}), .eq(comparator_1_eq));  // open: gt, lt
  Multiplexer #(.width(9)) multiplexer_1 (
    .in0(shifter_1_out), .in1({1'b0, Op}), .out({COut, Result}), .sel(comparator_1_eq));
endmodule

module ALU_Test (
);

  wire and_1_out, and_2_out, button_1_out, clock_1_out, comparator_1_eq, comparator_2_eq, or_1_out;
  wire [3:0] alu_1_result, alu_1_result_2, counter_1_q, counter_1_q_2, counter_1_q_3, counter_1_q_4,
       OP_CODE_data;
  wire [7:0] alu_1_flag_out, EXP_FLAGS_data, EXP_RES_data, FLAGS_IN_data, OP_A_data, OP_B_data;
  wire [23:16] counter_1_q_5;

  Hex_Digit_Display #(.decimalPoint("false")) hex_digit_display_1 (.value(counter_1_q_5[23:20]));
  Counter #(.max('hffffff), .trigger("falling"), .width(24)) counter_1 (
    .clk(or_1_out), .Q({counter_1_q_5, counter_1_q_4, counter_1_q_3, counter_1_q_2, counter_1_q}));  // open: clr, load, up, count, D, carry
  or or_1 (or_1_out, button_1_out, and_1_out);
  Clock clock_1 (.out(clock_1_out));
  Hex_Digit_Display #(.decimalPoint("false")) hex_digit_display_2 (.value(counter_1_q_4));
  Hex_Digit_Display #(.decimalPoint("false")) hex_digit_display_3 (.value(counter_1_q_5[19:16]));
  Button button_1 (.out(button_1_out));
  Hex_Digit_Display #(.decimalPoint("false")) hex_digit_display_4 (.value(counter_1_q_3));
  Hex_Digit_Display #(.decimalPoint("false")) hex_digit_display_5 (.value(counter_1_q_2));
  and and_1 (and_1_out, clock_1_out, and_2_out);
  Hex_Digit_Display #(.decimalPoint("false")) hex_digit_display_6 (.value(counter_1_q));
  LED led_1 (.in(and_2_out));
  ROM #(.addrWidth(24), .dataWidth(4)) OP_CODE (
    .addr({counter_1_q_5, counter_1_q_4, counter_1_q_3, counter_1_q_2, counter_1_q}), .data(OP_CODE_data));
  ROM #(.addrWidth(24)) OP_A (
    .addr({counter_1_q_5, counter_1_q_4, counter_1_q_3, counter_1_q_2, counter_1_q}), .data(OP_A_data));
  ROM #(.addrWidth(24)) OP_B (
    .addr({counter_1_q_5, counter_1_q_4, counter_1_q_3, counter_1_q_2, counter_1_q}), .data(OP_B_data));
  ROM #(.addrWidth(24)) FLAGS_IN (
    .addr({counter_1_q_5, counter_1_q_4, counter_1_q_3, counter_1_q_2, counter_1_q}), .data(FLAGS_IN_data));
  ROM #(.addrWidth(24)) EXP_RES (
    .addr({counter_1_q_5, counter_1_q_4, counter_1_q_3, counter_1_q_2, counter_1_q}), .data(EXP_RES_data));
  ROM #(.addrWidth(24)) EXP_FLAGS (
    .addr({counter_1_q_5, counter_1_q_4, counter_1_q_3, counter_1_q_2, counter_1_q}), .data(EXP_FLAGS_data));
  Comparator #(.mode("unsigned")) comparator_1 (
    .a({alu_1_result_2, alu_1_result}), .b(EXP_RES_data), .eq(comparator_1_eq));  // open: gt, lt
  Comparator #(.mode("unsigned")) comparator_2 (
    .a(alu_1_flag_out), .b(EXP_FLAGS_data), .eq(comparator_2_eq));  // open: gt, lt
  and and_2 (and_2_out, comparator_2_eq, comparator_1_eq);
  ALU alu_1 (
    .Flag_In(FLAGS_IN_data), .CMD_15_12(OP_CODE_data), .Op0(OP_A_data), .Op1(OP_B_data),
    .Result({alu_1_result_2, alu_1_result}), .Flag_Out(alu_1_flag_out));
  Hex_Digit_Display #(.decimalPoint("false")) hex_digit_display_7 (.value(alu_1_result_2));
  // LedBar #(.inputtype("row")) XXXXOCZ: pin names not known; wires that end beside it: alu_1_flag_out
  Hex_Digit_Display #(.decimalPoint("false")) hex_digit_display_8 (.value(alu_1_result));

  // Notes on the sheet:
  //   contents of OP_CODE (hex, n*v repeats v):
  //   4 195074*0 195075*1 195075*2 195075*3 195075*4 195075*5 195075*6 195075*9 195075*a 195075*b 195075*c
  //   195075*d 195075*e 195075*f
  //   contents of OP_A (hex, n*v repeats v):
  //   1 254*0 255*1 255*2 255*3 255*4 255*5 255*6 255*7 255*8 255*9 255*a 255*b 255*c 255*d 255*e 255*f
  //   255*10 255*11 255*12 255*13 255*14 255*15 255*16 255*17 255*18 255*19 255*1a 255*1b 255*1c 255*1d
  //   255*1e 255*1f 255*20 255*21 255*22 255*23 255*24 255*25 255*26 255*27 255*28 255*29 255*2a 255*2b
  //   255*2c 255*2d 255*2e 255*2f 255*30 255*31 255*32 255*33 255*34 255*35 255*36 255*37 255*38 255*39
  //   255*3a 255*3b 255*3c 255*3d 255*3e 255*3f 255*40 255*41 255*42 255*43 255*44 255*45 255*46 255*47
  //   255*48 255*49 255*4a 255*4b 255*4c 255*4d 255*4e 255*4f 255*50 255*51 255*52 255*53 255*54 255*55
  //   255*56 255*57 255*58 255*59 255*5a 255*5b 255*5c 255*5d 255*5e 255*5f 255*60 255*61 255*62 255*63
  //   255*64 255*65 255*66 255*67 255*68 255*69 255*6a 255*6b 255*6c 255*6d 255*6e 255*6f 255*70 255*71
  //   255*72 255*73 255*74 255*75 255*76 255*77 255*78 255*79 255*7a 255*7b 255*7c 255*7d 255*7e 255*7f
  //   255*80 255*81 255*82 255*83 255*84 255*85 255*86 255*87 255*88 255*89 255*8a 255*8b 255*8c 255*8d
  //   255*8e 255*8f 255*90 255*91 255*92 255*93 255*94 255*95 255*96 255*97 255*98 255*99 255*9a 255*9b
  //   255*9c 255*9d 255*9e 255*9f 255*a0 255*a1 255*a2 255*a3 255*a4 255*a5 255*a6 255*a7 255*a8 255*a9
  //   255*aa 255*ab 255*ac 255*ad 255*ae 255*af 255*b0 255*b1 255*b2 255*b3 255*b4 255*b5 255*b6 255*b7
  //   255*b8 255*b9 255*ba 255*bb 255*bc 255*bd 255*be 255*bf 255*c0 255*c1 255*c2 255*c3 255*c4 255*c5
  //   255*c6 255*c7 255*c8 255*c9 255*ca 255*cb 255*cc 255*cd 255*ce 255*cf 255*d0 255*d1 255*d2 255*d3
  //   255*d4 255*d5 255*d6 255*d7 255*d8 255*d9 255*da 255*db 255*dc 255*dd 255*de 255*df 255*e0 255*e1
  //   255*e2 255*e3 255*e4 255*e5 255*e6 255*e7 255*e8 255*e9 255*ea 255*eb 255*ec 255*ed 255*ee 255*ef
  //   255*f0 255*f1 255*f2 255*f3 255*f4 255*f5 255*f6 255*f7 255*f8 255*f9 255*fa 255*fb 255*fc 255*fd
  //   255*fe 255*0 255*1 255*2 255*3 255*4 255*5 255*6 255*7 255*8 255*9 255*a 255*b 255*c 255*d 255*e
  //   255*f 255*10 255*11 255*12 255*13 255*14 255*15 255*16 255*17 255*18 255*19 255*1a 255*1b 255*1c
  //   255*1d 255*1e 255*1f 255*20 255*21 255*22 255*23 255*24 255*25 255*26 255*27 255*28 255*29 255*2a
  //   255*2b 255*2c 255*2d 255*2e 255*2f 255*30 255*31 255*32 255*33 255*34 255*35 255*36 255*37 255*38
  //   255*39 255*3a 255*3b 255*3c 255*3d 255*3e 255*3f 255*40 255*41 255*42 255*43 255*44 255*45 255*46
  //   255*47 255*48 255*49 255*4a 255*4b 255*4c 255*4d 255*4e 255*4f 255*50 255*51 255*52 255*53 255*54
  //   255*55 255*56 255*57 255*58 255*59 255*5a 255*5b 255*5c 255*5d 255*5e 255*5f 255*60 255*61 255*62
  //   255*63 255*64 255*65 255*66 255*67 255*68 255*69 255*6a 255*6b 255*6c 255*6d 255*6e 255*6f 255*70
  //   255*71 255*72 255*73 255*74 255*75 255*76 255*77 255*78 255*79 255*7a 255*7b 255*7c 255*7d 255*7e
  //   255*7f 255*80 255*81 255*82 255*83 255*84 255*85 255*86 255*87 255*88 255*89 255*8a 255*8b 255*8c
  //   255*8d 255*8e 255*8f 255*90 255*91 255*92 255*93 255*94 255*95 255*96 255*97 255*98 255*99 255*9a
  //   255*9b 255*9c 255*9d 255*9e 255*9f 255*a0 255*a1 255*a2 255*a3 255*a4 255*a5 255*a6 255*a7 255*a8
  //   255*a9 255*aa 255*ab 255*ac 255*ad 255*ae 255*af 255*b0 255*b1 255*b2 255*b3 255*b4 255*b5 255*b6
  //   255*b7 255*b8 255*b9 255*ba 255*bb 255*bc 255*bd 255*be 255*bf 255*c0 255*c1 255*c2 255*c3 255*c4
  //   255*c5 255*c6 255*c7 255*c8 255*c9 255*ca 255*cb 255*cc 255*cd 255*ce 255*cf 255*d0 255*d1 255*d2
  //   255*d3 255*d4 255*d5 255*d6 255*d7 255*d8 255*d9 255*da 255*db 255*dc 255*dd 255*de 255*df 255*e0
  //   255*e1 255*e2 255*e3 255*e4 255*e5 255*e6 255*e7 255*e8 255*e9 255*ea 255*eb 255*ec 255*ed 255*ee
  //   255*ef 255*f0 255*f1 255*f2 255*f3 255*f4 255*f5 255*f6 255*f7 255*f8 255*f9 255*fa 255*fb 255*fc
  //   255*fd 255*fe 255*0 255*1 255*2 255*3 255*4 255*5 255*6 255*7 255*8 255*9 255*a 255*b 255*c 255*d
  //   255*e 255*f 255*10 255*11 255*12 255*13 255*14 255*15 255*16 255*17 255*18 255*19 255*1a 255*1b
  //   255*1c 255*1d 255*1e 255*1f 255*20 255*21 255*22 255*23 255*24 255*25 255*26 255*27 255*28 255*29
  //   255*2a 255*2b 255*2c 255*2d 255*2e 255*2f 255*30 255*31 255*32 255*33 255*34 255*35 255*36 255*37
  //   255*38 255*39 255*3a 255*3b 255*3c 255*3d 255*3e 255*3f 255*40 255*41 255*42 255*43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
  //   contents of OP_B (hex, n*v repeats v):
  //   0 1 2 3 4 5 6 7 8 9 a b c d e f 10 11 12 13 14 15 16 17 18 19 1a 1b 1c 1d 1e 1f 20 21 22 23 24 25 26
  //   27 28 29 2a 2b 2c 2d 2e 2f 30 31 32 33 34 35 36 37 38 39 3a 3b 3c 3d 3e 3f 40 41 42 43 44 45 46 47
  //   48 49 4a 4b 4c 4d 4e 4f 50 51 52 53 54 55 56 57 58 59 5a 5b 5c 5d 5e 5f 60 61 62 63 64 65 66 67 68
  //   69 6a 6b 6c 6d 6e 6f 70 71 72 73 74 75 76 77 78 79 7a 7b 7c 7d 7e 7f 80 81 82 83 84 85 86 87 88 89
  //   8a 8b 8c 8d 8e 8f 90 91 92 93 94 95 96 97 98 99 9a 9b 9c 9d 9e 9f a0 a1 a2 a3 a4 a5 a6 a7 a8 a9 aa
  //   ab ac ad ae af b0 b1 b2 b3 b4 b5 b6 b7 b8 b9 ba bb bc bd be bf c0 c1 c2 c3 c4 c5 c6 c7 c8 c9 ca cb
  //   cc cd ce cf d0 d1 d2 d3 d4 d5 d6 d7 d8 d9 da db dc dd de df e0 e1 e2 e3 e4 e5 e6 e7 e8 e9 ea eb ec
  //   ed ee ef f0 f1 f2 f3 f4 f5 f6 f7 f8 f9 fa fb fc fd fe 0 1 2 3 4 5 6 7 8 9 a b c d e f 10 11 12 13 14
  //   15 16 17 18 19 1a 1b 1c 1d 1e 1f 20 21 22 23 24 25 26 27 28 29 2a 2b 2c 2d 2e 2f 30 31 32 33 34 35
  //   36 37 38 39 3a 3b 3c 3d 3e 3f 40 41 42 43 44 45 46 47 48 49 4a 4b 4c 4d 4e 4f 50 51 52 53 54 55 56
  //   57 58 59 5a 5b 5c 5d 5e 5f 60 61 62 63 64 65 66 67 68 69 6a 6b 6c 6d 6e 6f 70 71 72 73 74 75 76 77
  //   78 79 7a 7b 7c 7d 7e 7f 80 81 82 83 84 85 86 87 88 89 8a 8b 8c 8d 8e 8f 90 91 92 93 94 95 96 97 98
  //   99 9a 9b 9c 9d 9e 9f a0 a1 a2 a3 a4 a5 a6 a7 a8 a9 aa ab ac ad ae af b0 b1 b2 b3 b4 b5 b6 b7 b8 b9
  //   ba bb bc bd be bf c0 c1 c2 c3 c4 c5 c6 c7 c8 c9 ca cb cc cd ce cf d0 d1 d2 d3 d4 d5 d6 d7 d8 d9 da
  //   db dc dd de df e0 e1 e2 e3 e4 e5 e6 e7 e8 e9 ea eb ec ed ee ef f0 f1 f2 f3 f4 f5 f6 f7 f8 f9 fa fb
  //   fc fd fe 0 1 2 3 4 5 6 7 8 9 a b c d e f 10 11 12 13 14 15 16 17 18 19 1a 1b 1c 1d 1e 1f 20 21 22 23
  //   24 25 26 27 28 29 2a 2b 2c 2d 2e 2f 30 31 32 33 34 35 36 37 38 39 3a 3b 3c 3d 3e 3f 40 41 42 43 44
  //   45 46 47 48 49 4a 4b 4c 4d 4e 4f 50 51 52 53 54 55 56 57 58 59 5a 5b 5c 5d 5e 5f 60 61 62 63 64 65
  //   66 67 68 69 6a 6b 6c 6d 6e 6f 70 71 72 73 74 75 76 77 78 79 7a 7b 7c 7d 7e 7f 80 81 82 83 84 85 86
  //   87 88 89 8a 8b 8c 8d 8e 8f 90 91 92 93 94 95 96 97 98 99 9a 9b 9c 9d 9e 9f a0 a1 a2 a3 a4 a5 a6 a7
  //   a8 a9 aa ab ac ad ae af b0 b1 b2 b3 b4 b5 b6 b7 b8 b9 ba bb bc bd be bf c0 c1 c2 c3 c4 c5 c6 c7 c8
  //   c9 ca cb cc cd ce cf d0 d1 d2 d3 d4 d5 d6 d7 d8 d9 da db dc dd de df e0 e1 e2 e3 e4 e5 e6 e7 e8 e9
  //   ea eb ec ed ee ef f0 f1 f2 f3 f4 f5 f6 f7 f8 f9 fa fb fc fd fe 0 1 2 3 4 5 6 7 8 9 a b c d e f 10 11
  //   12 13 14 15 16 17 18 19 1a 1b 1c 1d 1e 1f 20 21 22 23 24 25 26 27 28 29 2a 2b 2c 2d 2e 2f 30 31 32
  //   33 34 35 36 37 38 39 3a 3b 3c 3d 3e 3f 40 41 42 43 44 45 46 47 48 49 4a 4b 4c 4d 4e 4f 50 51 52 53
  //   54 55 56 57 58 59 5a 5b 5c 5d 5e 5f 60 61 62 63 64 65 66 67 68 69 6a 6b 6c 6d 6e 6f 70 71 72 73 74
  //   75 76 77 78 79 7a 7b 7c 7d 7e 7f 80 81 82 83 84 85 86 87 88 89 8a 8b 8c 8d 8e 8f 90 91 92 93 94 95
  //   96 97 98 99 9a 9b 9c 9d 9e 9f a0 a1 a2 a3 a4 a5 a6 a7 a8 a9 aa ab ac ad ae af b0 b1 b2 b3 b4 b5 b6
  //   b7 b8 b9 ba bb bc bd be bf c0 c1 c2 c3 c4 c5 c6 c7 c8 c9 ca cb cc cd ce cf d0 d1 d2 d3 d4 d5 d6 d7
  //   d8 d9 da db dc dd de df e0 e1 e2 e3 e4 e5 e6 e7 e8 e9 ea eb ec ed ee ef f0 f1 f2 f3 f4 f5 f6 f7 f8
  //   f9 fa fb fc fd fe 0 1 2 3 4 5 6 7 8 9 a b c d e f 10 11 12 13 14 15 16 17 18 19 1a 1b 1c 1d 1e 1f 20
  //   21 22 23 24 25 26 27 28 29 2a 2b 2c 2d 2e 2f 30 31 32 33 34 35 36 37 38 39 3a 3b 3c 3d 3e 3f 40 41
  //   42 43 44 45 46 47 48 49 4a 4b 4c 4d 4e 4f 50 51 52 53 54 55 56 57 58 59 5a 5b 5c 5d 5e 5f 60 61 62
  //   63 64 65 66 67 68 69 6a 6b 6c 6d 6e 6f 70 71 72 73 74 75 76 77 78 79 7a 7b 7c 7d 7e 7f 80 81 82 83
  //   84 85 86 87 88 89 8a 8b 8c 8d 8e 8f 90 91 92 93 94 95 96 97 98 99 9a 9b 9c 9d 9e 9f a0 a1 a2 a3 a4
  //   a5 a6 a7 a8 a9 aa ab ac ad ae af b0 b1 b2 b3 b4 b5 b6 b7 b8 b9 ba bb bc bd be bf c0 c1 c2 c3 c4 c5
  //   c6 c7 c8 c9 ca cb cc cd ce cf d0 d1 d2 d3 d4 d5 d6 d7 d8 d9 da db dc dd de df e0 e1 e2 e3 e4 e5 e6
  //   e7 e8 e9 ea eb ec ed ee ef f0 f1 f2 f3 f4 f5 f6 f7 f8 f9 fa fb fc fd fe 0 1 2 3 4 5 6 7 8 9 a b c d
  //   e f 10 11 12 13 14 15 16 17 18 19 1a 1b 1c 1d 1e 1f 20 21 22 23 24 25 26 27 28 29 2a 2b 2c 2d 2e 2f
  //   30 31 32 33 34 35 36 37 38 39 3a 3b 3c 3d 3e 3f 40 41 42 43 44 45 46 47 48 49 4a 4b 4c 4d 4e 4f 50
  //   51 52 53 54 55 56 57 58 59 5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
  //   contents of FLAGS_IN (hex, n*v repeats v):
  //   65025*0 65025*2 65025*7 65025*0 65025*2 65025*7 65025*0 65025*2 65025*7 65025*0 65025*2 65025*7
  //   65025*0 65025*2 65025*7 65025*0 65025*2 65025*7 65025*0 65025*2 65025*7 65025*0 65025*2 65025*7
  //   65025*0 65025*2 65025*7 65025*0 65025*2 65025*7 65025*0 65025*2 65025*7 65025*0 65025*2 65025*7
  //   65025*0 65025*2 65025*7 65025*0 65025*2 65025*7
  //   contents of EXP_RES (hex, n*v repeats v):
  //   0 1 2 3 4 5 6 7 8 9 a b c d e f 10 11 12 13 14 15 16 17 18 19 1a 1b 1c 1d 1e 1f 20 21 22 23 24 25 26
  //   27 28 29 2a 2b 2c 2d 2e 2f 30 31 32 33 34 35 36 37 38 39 3a 3b 3c 3d 3e 3f 40 41 42 43 44 45 46 47
  //   48 49 4a 4b 4c 4d 4e 4f 50 51 52 53 54 55 56 57 58 59 5a 5b 5c 5d 5e 5f 60 61 62 63 64 65 66 67 68
  //   69 6a 6b 6c 6d 6e 6f 70 71 72 73 74 75 76 77 78 79 7a 7b 7c 7d 7e 7f 80 81 82 83 84 85 86 87 88 89
  //   8a 8b 8c 8d 8e 8f 90 91 92 93 94 95 96 97 98 99 9a 9b 9c 9d 9e 9f a0 a1 a2 a3 a4 a5 a6 a7 a8 a9 aa
  //   ab ac ad ae af b0 b1 b2 b3 b4 b5 b6 b7 b8 b9 ba bb bc bd be bf c0 c1 c2 c3 c4 c5 c6 c7 c8 c9 ca cb
  //   cc cd ce cf d0 d1 d2 d3 d4 d5 d6 d7 d8 d9 da db dc dd de df e0 e1 e2 e3 e4 e5 e6 e7 e8 e9 ea eb ec
  //   ed ee ef f0 f1 f2 f3 f4 f5 f6 f7 f8 f9 fa fb fc fd fe 1 2 3 4 5 6 7 8 9 a b c d e f 10 11 12 13 14
  //   15 16 17 18 19 1a 1b 1c 1d 1e 1f 20 21 22 23 24 25 26 27 28 29 2a 2b 2c 2d 2e 2f 30 31 32 33 34 35
  //   36 37 38 39 3a 3b 3c 3d 3e 3f 40 41 42 43 44 45 46 47 48 49 4a 4b 4c 4d 4e 4f 50 51 52 53 54 55 56
  //   57 58 59 5a 5b 5c 5d 5e 5f 60 61 62 63 64 65 66 67 68 69 6a 6b 6c 6d 6e 6f 70 71 72 73 74 75 76 77
  //   78 79 7a 7b 7c 7d 7e 7f 80 81 82 83 84 85 86 87 88 89 8a 8b 8c 8d 8e 8f 90 91 92 93 94 95 96 97 98
  //   99 9a 9b 9c 9d 9e 9f a0 a1 a2 a3 a4 a5 a6 a7 a8 a9 aa ab ac ad ae af b0 b1 b2 b3 b4 b5 b6 b7 b8 b9
  //   ba bb bc bd be bf c0 c1 c2 c3 c4 c5 c6 c7 c8 c9 ca cb cc cd ce cf d0 d1 d2 d3 d4 d5 d6 d7 d8 d9 da
  //   db dc dd de df e0 e1 e2 e3 e4 e5 e6 e7 e8 e9 ea eb ec ed ee ef f0 f1 f2 f3 f4 f5 f6 f7 f8 f9 fa fb
  //   fc fd fe ff 2 3 4 5 6 7 8 9 a b c d e f 10 11 12 13 14 15 16 17 18 19 1a 1b 1c 1d 1e 1f 20 21 22 23
  //   24 25 26 27 28 29 2a 2b 2c 2d 2e 2f 30 31 32 33 34 35 36 37 38 39 3a 3b 3c 3d 3e 3f 40 41 42 43 44
  //   45 46 47 48 49 4a 4b 4c 4d 4e 4f 50 51 52 53 54 55 56 57 58 59 5a 5b 5c 5d 5e 5f 60 61 62 63 64 65
  //   66 67 68 69 6a 6b 6c 6d 6e 6f 70 71 72 73 74 75 76 77 78 79 7a 7b 7c 7d 7e 7f 80 81 82 83 84 85 86
  //   87 88 89 8a 8b 8c 8d 8e 8f 90 91 92 93 94 95 96 97 98 99 9a 9b 9c 9d 9e 9f a0 a1 a2 a3 a4 a5 a6 a7
  //   a8 a9 aa ab ac ad ae af b0 b1 b2 b3 b4 b5 b6 b7 b8 b9 ba bb bc bd be bf c0 c1 c2 c3 c4 c5 c6 c7 c8
  //   c9 ca cb cc cd ce cf d0 d1 d2 d3 d4 d5 d6 d7 d8 d9 da db dc dd de df e0 e1 e2 e3 e4 e5 e6 e7 e8 e9
  //   ea eb ec ed ee ef f0 f1 f2 f3 f4 f5 f6 f7 f8 f9 fa fb fc fd fe ff 0 3 4 5 6 7 8 9 a b c d e f 10 11
  //   12 13 14 15 16 17 18 19 1a 1b 1c 1d 1e 1f 20 21 22 23 24 25 26 27 28 29 2a 2b 2c 2d 2e 2f 30 31 32
  //   33 34 35 36 37 38 39 3a 3b 3c 3d 3e 3f 40 41 42 43 44 45 46 47 48 49 4a 4b 4c 4d 4e 4f 50 51 52 53
  //   54 55 56 57 58 59 5a 5b 5c 5d 5e 5f 60 61 62 63 64 65 66 67 68 69 6a 6b 6c 6d 6e 6f 70 71 72 73 74
  //   75 76 77 78 79 7a 7b 7c 7d 7e 7f 80 81 82 83 84 85 86 87 88 89 8a 8b 8c 8d 8e 8f 90 91 92 93 94 95
  //   96 97 98 99 9a 9b 9c 9d 9e 9f a0 a1 a2 a3 a4 a5 a6 a7 a8 a9 aa ab ac ad ae af b0 b1 b2 b3 b4 b5 b6
  //   b7 b8 b9 ba bb bc bd be bf c0 c1 c2 c3 c4 c5 c6 c7 c8 c9 ca cb cc cd ce cf d0 d1 d2 d3 d4 d5 d6 d7
  //   d8 d9 da db dc dd de df e0 e1 e2 e3 e4 e5 e6 e7 e8 e9 ea eb ec ed ee ef f0 f1 f2 f3 f4 f5 f6 f7 f8
  //   f9 fa fb fc fd fe ff 0 1 4 5 6 7 8 9 a b c d e f 10 11 12 13 14 15 16 17 18 19 1a 1b 1c 1d 1e 1f 20
  //   21 22 23 24 25 26 27 28 29 2a 2b 2c 2d 2e 2f 30 31 32 33 34 35 36 37 38 39 3a 3b 3c 3d 3e 3f 40 41
  //   42 43 44 45 46 47 48 49 4a 4b 4c 4d 4e 4f 50 51 52 53 54 55 56 57 58 59 5a 5b 5c 5d 5e 5f 60 61 62
  //   63 64 65 66 67 68 69 6a 6b 6c 6d 6e 6f 70 71 72 73 74 75 76 77 78 79 7a 7b 7c 7d 7e 7f 80 81 82 83
  //   84 85 86 87 88 89 8a 8b 8c 8d 8e 8f 90 91 92 93 94 95 96 97 98 99 9a 9b 9c 9d 9e 9f a0 a1 a2 a3 a4
  //   a5 a6 a7 a8 a9 aa ab ac ad ae af b0 b1 b2 b3 b4 b5 b6 b7 b8 b9 ba bb bc bd be bf c0 c1 c2 c3 c4 c5
  //   c6 c7 c8 c9 ca cb cc cd ce cf d0 d1 d2 d3 d4 d5 d6 d7 d8 d9 da db dc dd de df e0 e1 e2 e3 e4 e5 e6
  //   e7 e8 e9 ea eb ec ed ee ef f0 f1 f2 f3 f4 f5 f6 f7 f8 f9 fa fb fc fd fe ff 0 1 2 5 6 7 8 9 a b c d e
  //   f 10 11 12 13 14 15 16 17 18 19 1a 1b 1c 1d 1e 1f 20 21 22 23 24 25 26 27 28 29 2a 2b 2c 2d 2e 2f 30
  //   31 32 33 34 35 36 37 38 39 3a 3b 3c 3d 3e 3f 40 41 42 43 44 45 46 47 48 49 4a 4b 4c 4d 4e 4f 50 51
  //   52 53 54 55 56 57 58 59 5a 5b 5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
  //   contents of EXP_FLAGS (hex, n*v repeats v):
  //   1 381*0 4 253*0 4 4 126*0 3 125*0 4 4 4 125*0 3 2 124*0 4*4 124*0 3 2 2 123*0 5*4 123*0 3 2 2 2
  //   122*0 6*4 122*0 3 4*2 121*0 7*4 121*0 3 5*2 120*0 8*4 120*0 3 6*2 119*0 9*4 119*0 3 7*2 118*0 10*4
  //   118*0 3 8*2 117*0 11*4 117*0 3 9*2 116*0 12*4 116*0 3 10*2 115*0 13*4 115*0 3 11*2 114*0 14*4 114*0
  //   3 12*2 113*0 15*4 113*0 3 13*2 112*0 16*4 112*0 3 14*2 111*0 17*4 111*0 3 15*2 110*0 18*4 110*0 3
  //   16*2 109*0 19*4 109*0 3 17*2 108*0 20*4 108*0 3 18*2 107*0 21*4 107*0 3 19*2 106*0 22*4 106*0 3 20*2
  //   105*0 23*4 105*0 3 21*2 104*0 24*4 104*0 3 22*2 103*0 25*4 103*0 3 23*2 102*0 26*4 102*0 3 24*2
  //   101*0 27*4 101*0 3 25*2 100*0 28*4 100*0 3 26*2 99*0 29*4 99*0 3 27*2 98*0 30*4 98*0 3 28*2 97*0
  //   31*4 97*0 3 29*2 96*0 32*4 96*0 3 30*2 95*0 33*4 95*0 3 31*2 94*0 34*4 94*0 3 32*2 93*0 35*4 93*0 3
  //   33*2 92*0 36*4 92*0 3 34*2 91*0 37*4 91*0 3 35*2 90*0 38*4 90*0 3 36*2 89*0 39*4 89*0 3 37*2 88*0
  //   40*4 88*0 3 38*2 87*0 41*4 87*0 3 39*2 86*0 42*4 86*0 3 40*2 85*0 43*4 85*0 3 41*2 84*0 44*4 84*0 3
  //   42*2 83*0 45*4 83*0 3 43*2 82*0 46*4 82*0 3 44*2 81*0 47*4 81*0 3 45*2 80*0 48*4 80*0 3 46*2 79*0
  //   49*4 79*0 3 47*2 78*0 50*4 78*0 3 48*2 77*0 51*4 77*0 3 49*2 76*0 52*4 76*0 3 50*2 75*0 53*4 75*0 3
  //   51*2 74*0 54*4 74*0 3 52*2 73*0 55*4 73*0 3 53*2 72*0 56*4 72*0 3 54*2 71*0 57*4 71*0 3 55*2 70*0
  //   58*4 70*0 3 56*2 69*0 59*4 69*0 3 57*2 68*0 60*4 68*0 3 58*2 67*0 61*4 67*0 3 59*2 66*0 62*4 66*0 3
  //   60*2 65*0 63*4 65*0 3 61*2 64*0 64*4 64*0 3 62*2 63*0 65*4 63*0 3 63*2 62*0 66*4 62*0 3 64*2 61*0
  //   67*4 61*0 3 65*2 60*0 68*4 60*0 3 66*2 59*0 69*4 59*0 3 67*2 58*0 70*4 58*0 3 68*2 57*0 71*4 57*0 3
  //   69*2 56*0 72*4 56*0 3 70*2 55*0 73*4 55*0 3 71*2 54*0 74*4 54*0 3 72*2 53*0 75*4 53*0 3 73*2 52*0
  //   76*4 52*0 3 74*2 51*0 77*4 51*0 3 75*2 50*0 78*4 50*0 3 76*2 49*0 79*4 49*0 3 77*2 48*0 80*4 48*0 3
  //   78*2 47*0 81*4 47*0 3 79*2 46*0 82*4 46*0 3 80*2 45*0 83*4 45*0 3 81*2 44*0 84*4 44*0 3 82*2 43*0
  //   85*4 43*0 3 83*2 42*0 86*4 42*0 3 84*2 41*0 87*4 41*0 3 85*2 40*0 88*4 40*0 3 86*2 39*0 89*4 39*0 3
  //   87*2 38*0 90*4 38*0 3 88*2 37*0 91*4 37*0 3 89*2 36*0 92*4 36*0 3 90*2 35*0 93*4 35*0 3 91*2 34*0
  //   94*4 34*0 3 92*2 33*0 95*4 33*0 3 93*2 32*0 96*4 32*0 3 94*2 31*0 97*4 31*0 3 95*2 30*0 98*4 30*0 3
  //   96*2 29*0 99*4 29*0 3 97*2 28*0 100*4 28*0 3 98*2 27*0 101*4 27*0 3 99*2 26*0 102*4 26*0 3 100*2
  //   25*0 103*4 25*0 3 101*2 24*0 104*4 24*0 3 102*2 23*0 105*4 23*0 3 103*2 22*0 106*4 22*0 3 104*2 21*0
  //   107*4 21*0 3 105*2 20*0 108*4 20*0 3 106*2 19*0 109*4 19*0 3 107*2 18*0 110*4 18*0 3 108*2 17*0
  //   111*4 17*0 3 109*2 16*0 112*4 16*0 3 110*2 15*0 113*4 15*0 3 111*2 14*0 114*4 14*0 3 112*2 13*0
  //   115*4 13*0 3 113*2 12*0 116*4 12*0 3 114*2 11*0 117*4 11*0 3 115*2 10*0 118*4 10*0 3 116*2 9*0 119*4
  //   9*0 3 117*2 8*0 120*4 8*0 3 118*2 7*0 121*4 7*0 3 119*2 6*0 122*4 6*0 3 120*2 5*0 123*4 5*0 3 121*2
  //   4*0 124*4 4*0 3 122*2 0 0 0 125*4 0 0 0 3 123*2 0 0 126*4 0 0 3 124*2 0 127*4 0 3 125*2 128*0 7
  //   126*6 127*0 3 127*6 126*0 3 2 126*6 2 125*0 3 2 2 125*6 2 2 124*0 3 2 2 2 124*6 2 2 2 123*0 3 4*2
  //   123*6 4*2 122*0 3 5*2 122*6 5*2 121*0 3 6*2 121*6 6*2 120*0 3 7*2 120*6 7*2 119*0 3 8*2 119*6 8*2
  //   118*0 3 9*2 118*6 9*2 117*0 3 10*2 117*6 10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
endmodule

module ALU_TEST_CI (
  output halt,
  output [23:0] ADDR,
  output [7:0] Result,
  output [7:0] Flags
);

  wire and_1_out, and_3_out, clock_1_out, comparator_1_eq, comparator_2_eq;
  wire [43:0] ram_1_dout;

  Counter #(.max('hffffff), .width(24)) counter_1 (.clk(and_1_out), .Q(ADDR));  // open: clr, load, up, count, D, carry
  Clock clock_1 (.out(clock_1_out));
  and and_1 (and_1_out, clock_1_out, and_3_out);
  LED OK (.in(and_3_out));
  and and_2 (halt, ~and_3_out, clock_1_out);  // AND_Gate
  RAM #(.addrWidth(24), .dataWidth(44), .trigger("falling")) ram_1 (
    .addr(ADDR), .clk(clock_1_out), .dout(ram_1_dout));  // open: we, oe, din
  ALU alu_1 (
    .Flag_In(ram_1_dout[23:16]), .CMD_15_12(ram_1_dout[43:40]), .Op0(ram_1_dout[39:32]),
    .Op1(ram_1_dout[31:24]), .Result(Result), .Flag_Out(Flags));
  Hex_Digit_Display #(.decimalPoint("false")) hex_digit_display_1 (.value(Result[7:4]));
  Hex_Digit_Display #(.decimalPoint("false")) hex_digit_display_2 (.value(Result[3:0]));
  Comparator #(.mode("unsigned")) comparator_1 (
    .a(Result), .b(ram_1_dout[15:8]), .eq(comparator_1_eq));  // open: gt, lt
  and and_3 (and_3_out, comparator_1_eq, comparator_2_eq);
  // LedBar #(.inputtype("row")) XXXXOCZ: pin names not known; wires that end beside it: Flags
  Comparator #(.mode("unsigned")) comparator_2 (.a(Flags), .b(ram_1_dout[7:0]), .eq(comparator_2_eq));  // open: gt, lt
endmodule
